# Fritzing sketch schematics (saved by Fritzing 0.9.4)
breadboards: 1

parts:
  U1 = NodeMCU V3.0
  Part1 = Adafruit Pro Trinket 5V 16MHz [part_number="Adafruit #2000"]
  LED1 = smd LED [color="Red (633nm)" package="0603 [SMD]"]
  R1 = Resistor [tolerance=±5% resistance=220 package="0402 [SMD]"]

nets:
  N1: U1.D1, Part1.D12, LED1.cathode
  N2: U1.GND#6, U1.GND#13, U1.GND#16, U1.GND#33, Part1.GND, R1.Pin_1
  VIN: U1.Vin, Part1.+5V
  N3: LED1.anode, R1.Pin_0

custom parts:
  NodeMCU V3.0: ESP8266 based NodeMCU
  Adafruit Pro Trinket 5V 16MHz: Trinket's got a big sister in town - the Pro Trinket 5V! Pro Trinket combines everything you love about Trinket with the familiarity of the common core Arduino chip, the ATmega328. It's like an Arduino Pro Mini with more pins and USB tossed in, so delicious. Trinket's a year old now, and while its been great to see tons of tiny projects, sometimes you just need more pins, more FLASH, and more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
